// Digital circuit 8NOR.dig as structural Verilog
module _8NOR (
  input  in_1,
  input  in_2,
  input  in_3,
  input  in_4,
  input  in_5,
  input  in_6,
  input  in_7,
  input  in_8,
  output out_9
);

  wire nand_1_out, nor_1_out, nor_2_out;

  nor nor_1 (nor_1_out, in_1, in_2, in_3, in_4);
  nor nor_2 (nor_2_out, in_5, in_6, in_7, in_8);
  nand nand_1 (nand_1_out, nor_1_out, nor_2_out);
  not not_1 (out_9, nand_1_out);
endmodule
