// Digital circuit 9NOR-OR.dig as structural Verilog
module _9NOR_OR (
  input  in_1,
  input  in_2,
  input  in_3,
  input  in_4,
  input  in_5,
  input  in_6,
  input  in_7,
  input  in_8,
  input  in_9,
  output out_10
);

  wire nor_1_out, nor_2_out, nor_3_out;

  nor nor_1 (nor_1_out, in_1, in_2, in_3);
  nor nor_2 (nor_2_out, in_4, in_8, in_9);
  nor nor_3 (nor_3_out, in_5, in_6, in_7);
  or or_1 (out_10, nor_1_out, nor_2_out, nor_3_out);
endmodule
