// Digital circuit DFFS.dig as structural Verilog
module DFFS (
  input  IN,
  input  C,
  input  C_INV,
  output OUT
);

  wire multiplexer_1_out;

  Multiplexer multiplexer_1 (.sel(C), .in_0(multiplexer_1_out), .in_1(IN), .out(multiplexer_1_out));
  Multiplexer multiplexer_2 (.sel(C_INV), .in_0(OUT), .in_1(multiplexer_1_out), .out(OUT));
endmodule
