// Digital circuit DFF_ALR_CLK.dig as structural Verilog
module DFF_ALR_CLK (
  input  in_2,
  input  in_3,
  input  in_4,
  output out_1
);

  wire multiplexer_1_out, multiplexer_2_out, nand_1_out, nand_2_out, not_1_out, not_3_out;

  nand nand_1 (nand_1_out, multiplexer_2_out, in_2);
  not not_1 (not_1_out, nand_1_out);
  Multiplexer multiplexer_1 (.sel(not_3_out), .in_0(nand_1_out), .in_1(nand_2_out), .out(multiplexer_1_out));
  nand nand_2 (nand_2_out, in_2, out_1);
  Multiplexer multiplexer_2 (.sel(not_3_out), .in_0(not_1_out), .in_1(in_3), .out(multiplexer_2_out));
  not not_2 (out_1, multiplexer_1_out);
  not not_3 (not_3_out, in_4);
endmodule
