// Digital circuit dflipflip_active_low_reset.dig as structural Verilog
module dflipflip_active_low_reset (
  input  in_3,
  input  Reset__top__active_low,
  input  in_5,
  output out_1,
  output out_2
);

  wire multiplexer_1_out, multiplexer_2_out, nand_2_out, not_1_out;

  Multiplexer multiplexer_1 (.sel(in_5), .in_0(in_3), .in_1(not_1_out), .out(multiplexer_1_out));
  nand nand_1 (out_1, out_2, Reset__top__active_low);
  nand nand_2 (nand_2_out, Reset__top__active_low, multiplexer_1_out);
  not not_1 (not_1_out, nand_2_out);
  not not_2 (out_2, multiplexer_2_out);
  Multiplexer multiplexer_2 (.sel(in_5), .in_0(out_1), .in_1(nand_2_out), .out(multiplexer_2_out));

  // Notes on the sheet:
  //   Data (b)
  //   Clock (B)
  //   Out (2)
  //   Inverted output 3
endmodule
