// Digital circuit DFF_E.dig as structural Verilog
module DFF_E (
  input  in_1,
  input  in_2,
  output out_3
);

  wire multiplexer_1_out, multiplexer_2_out, not_1_out, not_2_out, not_3_out, not_5_out;

  not not_1 (not_1_out, multiplexer_2_out);
  not not_2 (not_2_out, not_1_out);
  Multiplexer multiplexer_1 (.sel(not_5_out), .in_0(not_1_out), .in_1(not_3_out), .out(multiplexer_1_out));
  not not_3 (not_3_out, out_3);
  not not_4 (out_3, multiplexer_1_out);
  Multiplexer multiplexer_2 (.sel(not_5_out), .in_0(not_2_out), .in_1(in_2), .out(multiplexer_2_out));
  not not_5 (not_5_out, in_1);

  // Notes on the sheet:
  //   Data (input bottom)
  //   Clock (Input top)
endmodule
