// Digital circuit DFFTR.dig as structural Verilog
module DFFTR (
  input  IN,
  input  C,
  input  C_INV,
  input  CONN,
  output OUT
);

  wire multiplexer_1_out, multiplexer_2_out;

  Multiplexer multiplexer_1 (.sel(C), .in_0(multiplexer_1_out), .in_1(IN), .out(multiplexer_1_out));
  Multiplexer multiplexer_2 (.sel(C_INV), .in_0(multiplexer_2_out), .in_1(multiplexer_1_out), .out(multiplexer_2_out));
  assign OUT = CONN ? multiplexer_2_out : 1'bz;  // Driver driver_1
endmodule
