// Digital circuit LATCH.dig as structural Verilog
module LATCH (
  input  in_1,
  input  in_2,
  output out_3
);

  wire not_1_out, not_2_out;

  not not_1 (not_1_out, not_2_out);
  Multiplexer multiplexer_1 (.sel(in_2), .in_0(not_1_out), .in_1(in_1), .out(out_3));
  not not_2 (not_2_out, out_3);

  // Notes on the sheet:
  //   In
  //   Clk
endmodule
