// Digital circuit LATCHI.dig as structural Verilog
module LATCHI (
  input  in_1,
  input  in_2,
  output out_3
);

  wire multiplexer_1_out, not_1_out;

  not not_1 (not_1_out, out_3);
  Multiplexer multiplexer_1 (.sel(in_2), .in_0(not_1_out), .in_1(in_1), .out(multiplexer_1_out));
  not not_2 (out_3, multiplexer_1_out);

  // Notes on the sheet:
  //   In
  //   Clk
endmodule
