// Digital circuit LATCHSTR.dig as structural Verilog
module LATCHSTR (
  input  CLK,
  input  IN,
  input  CONN,
  output OUT
);

  wire multiplexer_1_out, not_1_out, not_2_out;

  not not_1 (not_1_out, not_2_out);
  Multiplexer multiplexer_1 (.sel(CLK), .in_0(not_1_out), .in_1(IN), .out(multiplexer_1_out));
  not not_2 (not_2_out, multiplexer_1_out);
  assign OUT = CONN ? multiplexer_1_out : 1'bz;  // Driver driver_1
endmodule
