// Digital circuit logic.dig as structural Verilog
module \logic  (
  input  A,
  input  B,
  input  C,
  input  D,
  output Q
);

  wire nand_1_out, nor_1_out;

  nand nand_1 (nand_1_out, C, D);
  nor nor_1 (nor_1_out, A, B);
  and and_1 (Q, nor_1_out, nand_1_out);
endmodule
