// Digital circuit OAI21.dig as structural Verilog
module OAI21 (
  input  in_2,
  input  in_3,
  input  in_4,
  output out_1
);

  wire and_1_out, or_1_out;

  or or_1 (or_1_out, in_2, in_3);
  and and_1 (and_1_out, or_1_out, in_4);
  not not_1 (out_1, and_1_out);

  // Notes on the sheet:
  //   A
  //   B
  //   C
endmodule
